# Fritzing sketch Vbe_Check_JFET (saved by Fritzing 0.9.3b)
breadboards: 1

parts:
  R1 = Resistor [tolerance=±5% resistance=1.2k package=THT]
  Q1 = NPN-Transistor [package="TO92 [THT]"]
  R2 = Resistor [tolerance=±5% resistance=330 package=THT]
  R4 = TRIMPOT [package=trimpot_pth_s3_lock]
  Q2 = Basic FET N-Channel [package="TO220 [THT]"]
  R5 = Resistor [tolerance=±5% resistance=100 package=THT]

nets:
  N1: R1.Pin_0, Q1.C, R2.Pin_1
  N2: R1.Pin_1, Q1.B
  N3: Q1.E, Q2.gate
  N4: R2.Pin_0, Q2.drain, R5.Pin_0
  N5: R4.CCW, Q2.source
  N6: R4.WIPER, R4.CW, R5.Pin_1

notes:
  GND
  +9V
  2SK170GR
  D / G / S
  VMeter
  2SC1815
  E / C / B
